# Fritzing sketch  Riego (saved by Fritzing 0.9.2b)
breadboards: 1

parts:
  Power_plug1 = Power plug
  KY-1 = Keyes Relay [package=THT]
  Part2 = Arduino Nano (Rev3.0)
  VALVE1 = Plastic Solenoid Valve

nets:
  GND: Power_plug1.GND, KY-1.ground, Part2.GND, VALVE1.no_name_yet#2
  VCC: Power_plug1.VCC, KY-1.power, KY-1.NO, Part2.VIN
  N1: KY-1.signal, Part2.D11/MOSI
  N2: KY-1.C, VALVE1.no_name_yet#1

custom parts:
  Keyes Relay: The Keyes 5V relay module is suitable for SCM development, home appliance control. It uses a 5V~12V TIL control signal which can control DC / AC signal.

// code stored in the sketch: Riego2.ino
int PinValvula = 11;     // equivale al pin digital 3 "http://robotshop.com/letsmakerobots//files/field_primary_image/NanoAnalogPinChanges.resized.jpg"

void setup() { 

  // setear el pin de valvula como salida
  pinMode(PinValvula, OUTPUT);    

}

void loop(){
  digitalWrite(PinValvula, HIGH); // abre la valvula
  delay(1000);    // espera 10 segundos
  digitalWrite(PinValvula, LOW); //apaga la valvula
  delay(1000); 
}
