# Fritzing sketch  RiegoPotent (saved by Fritzing 0.9.2b)
circuit board: 5.77131cm x 5.23964cm
breadboards: 1

parts:
  Power_plug1 = Power plug
  KY-1 = Keyes Relay [package=THT]
  Part2 = Arduino Nano (Rev3.0)
  VALVE1 = Plastic Solenoid Valve
  Part3 = FC-28 Soil Hygrometer Module
  R1 = Rotary Potentiometer (Small) [maximum_resistance=100kΩ package=THT]

nets:
  GND: Power_plug1.GND, KY-1.ground, Part2.GND, VALVE1.no_name_yet#2, Part3.GND, R1.wiper
  VCC: Power_plug1.VCC, KY-1.power, KY-1.NO, Part2.VIN
  N1: KY-1.signal, Part2.D11/MOSI
  N2: KY-1.C, VALVE1.no_name_yet#1
  5V: Part2.5V, Part3.VCC
  N3: Part2.A1, R1.leg1
  N4: Part2.A0, Part3.AO

custom parts:
  Keyes Relay: The Keyes 5V relay module is suitable for SCM development, home appliance control. It uses a 5V~12V TIL control signal which can control DC / AC signal.
  FC-28 Soil Hygrometer Module: The FC-28 is a soil hygrometer module that uses the Texas Instruments LM393 comparator chip to provide an analog measurement of soil humidity. The digital output is high when soil moisture is over a certain threshold, as determined by adjusting the potentiometer.

// code stored in the sketch: Riego2.ino
int PinValvula = 11;     // equivale al pin digital 11 "http://robotshop.com/letsmakerobots//files/field_primary_image/NanoAnalogPinChanges.resized.jpg"

void setup() { 

  // setear el pin de valvula como salida
  pinMode(PinValvula, OUTPUT);    
  Serial.begin(9600); 
}

void loop(){
  int sensorValue = analogRead(A0);
	int threshold = analogRead(A1)
  if (sensorValue >= threshold)
  {
    digitalWrite(PinValvula, HIGH); // abre la valvula
  }
  else if (sensorValue < threshold){
    digitalWrite(PinValvula, LOW); //apaga la valvula
  }
  delay(1000); 
  Serial.print(sensorValue);
}
